# Fritzing sketch Nano_ESP_RGB (saved by Fritzing 0.9.3b)
breadboards: 1

parts:
  Součástka1 = Arduino Nano (Rev3.0) (ICSP)
  LPD8806_RGB_LED_Strip1 = LPD8806 RGB LED Strip
  WeMos_D1_Mini1 = WeMos D1 Mini

nets:
  GND: Součástka1.GND, LPD8806_RGB_LED_Strip1.GND, WeMos_D1_Mini1.G
  N1: Součástka1.D6, LPD8806_RGB_LED_Strip1.DI
  5V: Součástka1.5V, LPD8806_RGB_LED_Strip1.+5V
  N2: Součástka1.A5, WeMos_D1_Mini1.D1
  N3: Součástka1.A4, WeMos_D1_Mini1.D2
  3V3: Součástka1.3V3, WeMos_D1_Mini1.3V3

custom parts:
  LPD8806 RGB LED Strip: Digitally addressable RGB LED strip
